# Fritzing sketch layout (saved by Fritzing 0.9.3b)

parts:
  L298N1 = L298N DC motor driver
  M1 = DC Motor
  M3 = fc-51 [package=THT]
  M4 = fc-51 [package=THT]
  U1 = ESP8266 NodeMCU LoLin module
  M5 = DC Motor
  R1 = Resistor [tolerance=±5% resistance=10 package=THT]
  VCC1 = Battery block 9V

nets:
  N1: L298N1.OUT1, M5.pin_2
  N2: L298N1.OUT2, M5.pin_1
  N3: L298N1.OUT3, M1.pin_2
  N4: L298N1.OUT4, M1.pin_1
  N5: L298N1.12V, R1.Pin_1
  GND: L298N1.GND, M3.pin2, M4.pin2, U1.GND, VCC1.-
  N6: L298N1.5V#9, U1.D5
  N7: L298N1.5V#10, U1.D6
  N8: L298N1.IN1, U1.D7
  N9: L298N1.IN2, U1.D8
  N10: L298N1.IN3, U1.D4
  N11: L298N1.IN4, U1.D3
  N12: M3.pin1, U1.D0
  N13: M3.pin3, M4.pin3, U1.3V3
  N14: M4.pin1, U1.D1
  N15: U1.Vin, R1.Pin_0

custom parts:
  L298N DC motor driver: 2x DC motor driver with 78M05 positive voltage regulator (7..35 V) L298N: max 46 V, 2 A Set 5 V Enable jumper to enable 5 V regultor (needed for the L298N) and +5 V output at screw terminal or supply external +5 V at screw terminal Set ENA and/or ENB to +5 V to enable motor permanently or supply ENA and/or ENB with PWM signal IN1 and IN2 set rotation directory for motor A (OUT1/OUT2) IN2 and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
  ESP8266 NodeMCU LoLin module: ESP8266 based NodeMCU
